# Fritzing sketch external_diagram (saved by Fritzing 0.9.3b)
stripboards: 1

parts:
  LED1 = smd LED [color="Red (633nm)" package="0805 [SMD]"]
  LED2 = smd LED [color="Red (633nm)" package="0805 [SMD]"]
  LED3 = smd LED [color="Red (633nm)" package="0805 [SMD]"]
  LED4 = smd LED [color="Red (633nm)" package="0805 [SMD]"]
  LED5 = smd LED [color="Red (633nm)" package="0805 [SMD]"]
  R1 = Resistor [tolerance=±5% resistance=220 package="0402 [SMD]"]
  R2 = Resistor [tolerance=±5% resistance=220 package="0603 [SMD]"]
  R3 = Resistor [tolerance=±5% resistance=220 package="0603 [SMD]"]
  R4 = Resistor [tolerance=±5% resistance=220 package=THT]
  R5 = Resistor [tolerance=±5% resistance=220 package=THT]
  Part1 = Arduino Nano (Rev3.0)
  Part2 = Logic Level Converter
  R6 = Resistor [tolerance=±5% resistance=1k package=THT]

nets:
  GND: LED1.cathode, LED2.cathode, LED3.cathode, LED4.cathode, LED5.cathode, Part1.GND, Part2.GND
  N1: LED1.anode, R1.Pin_0
  N2: LED2.anode, R2.Pin_0
  N3: LED3.anode, R3.Pin_0
  N4: LED4.anode, R4.Pin_0
  N5: LED5.anode, R5.Pin_0
  N6: R1.Pin_1, Part1.D2
  N7: R2.Pin_1, Part1.D3
  N8: R3.Pin_1, Part1.D4
  N9: R4.Pin_1, Part1.D5
  N10: R5.Pin_1, Part1.D6
  N11: Part1.D7, Part2.TX2_HV
  N12: Part1.D8, Part2.RX2_HV
  N13: Part1.5V, Part2.HV
  N14: Part1.3V3, Part2.LV, R6.Pin_0
  N15: Part2.TX2_LV, R6.Pin_1
  N16: Part2.TX_HV, Part2.RX_HV

notes:
  These connect to the controller-side cable (the side with the port)
  One end of the resistor should be in TXI and the other should be in LV (fritzing just makes the resistors too big)
  Pin 1: White: 5V
  Pin 2: Red: Data
  Pin 3: Black: Ground
  Pin 4: Yellow: Ground
  Pin 5: Green: 3.43V
  These connect to the console-side cable (the side with the the plug)
